# Fritzing sketch mpu6050 (saved by Fritzing 0.9.3b)
breadboards: 1

parts:
  GY1 = MPU-6050 Board GY-521 [form="♀ (female)" package=THT]
  パーツ1 = Arduino Uno (Rev3)

nets:
  N1: GY1.pin1, パーツ1.3V3
  N2: GY1.pin2, パーツ1.GND
  N3: GY1.pin3, パーツ1.A5/SCL
  N4: GY1.pin4, パーツ1.A4/SDA

custom parts:
  MPU-6050 Board GY-521: Acelerometro y Giroscopio MPU-6050 Board GY-521
